# Fritzing sketch Design (saved by Fritzing 0.9.3b)
circuit board: 8.46667cm x 5.64444cm
breadboards: 1

parts:
  LCD1 = LCD screen
  Part1 = Arduino Pro Mini (3.3V)
  DS1 = DS18B20 1-Wire Temperature Sensor [part_number=DS18B20]
  V1 = DC Power [voltage=5]
  R1 = Resistor [tolerance=±5% resistance=4.7k package="0603 [SMD]"]

nets:
  GND: LCD1.VSS, LCD1.R/W, Part1.GND, DS1.GND, V1.V-
  VDD: LCD1.VDD, Part1.VCC, DS1.VDD, V1.V+, R1.Pin_0
  N1: LCD1.RS, Part1.MOSI
  N2: LCD1.E, Part1.MISO
  N3: LCD1.DB4, Part1.D5
  N4: LCD1.DB5, Part1.D4
  N5: LCD1.DB6, Part1.D3
  N6: LCD1.DB7, Part1.D2
  N7: Part1.D6, DS1.DQ, R1.Pin_1
